# Fritzing sketch HomePrototypeLayout (saved by Fritzing 0.9.3b)
breadboards: 1

parts:
  Part1 = Adafruit Feather 32u4 Bluefruit [part_number="Adafruit #2829"]
  R1 = Resistor [tolerance=±1% resistance=5.1k package=THT]
  R2 = TRIMPOT [package=3386u]
  R3 = Resistor [tolerance=±1% resistance=5.1k package=THT]
  Part2 = 12 NeoPixel Ring [part_number=1643]
  Part3 = Lithium Ion Polymer Battery 3.7v 500mAh [part_number=1578]
  IC2 = DIP - 8 pins [part_number=1223019V5 chip_label="DP Sensor Breakout Board" package="DIP (Dual Inline) [THT]"]

nets:
  N1: Part1.A4, R2.WIPER
  GND: Part1.GND, R2.CCW, Part2.GND, Part3.negative, IC2.GND
  VDD: Part1.+3V3, R1.Pin_0, R2.CW, R3.Pin_0, Part2.VDD, IC2.VDD
  N2: Part1.VBAT, Part3.positive
  N3: Part1.6, Part2.IN
  N4: Part1.3, R1.Pin_1, IC2.SCL
  N5: Part1.2, R3.Pin_1, IC2.SDA

custom parts:
  Adafruit Feather 32u4 Bluefruit: This is the Adafruit Feather 32u4 Bluefruit - our take on an 'all-in-one' Arduino-compatible + Bluetooth Low Energy with built in USB and battery charging. Its an Adafruit Feather 32u4 with a BTLE module, ready to rock! We have other boards in the Feather family, check'em out here. Bluetooth Low Energy is the hottest new low-power, 2.4GHz spectrum wireless protocol. In particular, its the only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
  12 NeoPixel Ring: 12 ultra bright smart LED NeoPixels are arranged in a circle with 1.5" (37mm) outer diameter. The rings are 'chainable' - connect the output pin of one to the input pin of another. Use only one microcontroller pin to control as many as you can chain together! Each LED is addressable as the driver chip is inside the LED. Each one has ~18mA constant current drive so the color will be very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
  Lithium Ion Polymer Battery 3.7v 500mAh: Lithium ion polymer (also known as 'lipo' or 'lipoly') batteries are thin, light and powerful. The output ranges from 4.2V when completely charged to 3.7V. This battery has a capacity of 500mAh for a total of about 1.9 Wh. The batteries come pre-attached with a genuine 2-pin JST-PH connector as shown and include the necessary protection circuitry.
  DIP - 8 pins: Sensor SDP31 Breakout board with I2C interface.
